// Logisim project H3.circ as structural Verilog: 1 circuit, main circuit main
module main (
  input  Input,
  output Output,
  output out_3,
  output Current_State,
  output out_5
);

  wire _0_000_out, _0_001_out, _0_010_out, _0_011_out, _0_100_out, _1_000_out, _1_001_out, _1_010_out,
       _1_011_out, _1_100_out, clock_1_out, not_1_out, not_2_out, not_3_out, not_4_out, not_5_out, not_6_out,
       not_7_out, not_8_out, not_9_out, not_10_out, not_11_out, not_12_out, not_13_out, not_14_out,
       not_15_out, not_16_out, not_17_out, not_18_out, not_19_out, not_20_out, not_21_out, not_22_out,
       not_23_out, not_24_out, not_25_out, S1_out, S2_out, S3_out;

  Clock clock_1 (.out(clock_1_out));
  not not_1 (not_1_out, Input);
  not not_2 (not_2_out, out_3);
  not not_3 (not_3_out, Current_State);
  not not_4 (not_4_out, out_5);
  not not_5 (not_5_out, out_3);
  not not_6 (not_6_out, Current_State);
  not not_7 (not_7_out, out_5);
  not not_8 (not_8_out, Input);
  not not_9 (not_9_out, out_3);
  not not_10 (not_10_out, Current_State);
  not not_11 (not_11_out, out_3);
  not not_12 (not_12_out, Current_State);
  not not_13 (not_13_out, Input);
  not not_14 (not_14_out, out_3);
  not not_15 (not_15_out, out_5);
  not not_16 (not_16_out, out_3);
  not not_17 (not_17_out, out_5);
  not not_18 (not_18_out, Input);
  not not_19 (not_19_out, out_3);
  not not_20 (not_20_out, out_3);
  not not_21 (not_21_out, Input);
  not not_22 (not_22_out, Current_State);
  not not_23 (not_23_out, out_5);
  not not_24 (not_24_out, Current_State);
  not not_25 (not_25_out, out_5);
  and _0_000 (_0_000_out, not_1_out, not_2_out, not_3_out, not_4_out);
  and _1_000 (_1_000_out, Input, not_5_out, not_6_out, not_7_out);
  and _0_001 (_0_001_out, not_8_out, not_9_out, not_10_out, out_5);
  and _1_001 (_1_001_out, Input, not_11_out, not_12_out, out_5);
  and _0_010 (_0_010_out, not_13_out, not_14_out, Current_State, not_15_out);
  and _1_010 (_1_010_out, Input, not_16_out, Current_State, not_17_out);
  and _0_011 (_0_011_out, not_18_out, not_19_out, Current_State, out_5);
  and _1_011 (_1_011_out, Input, not_20_out, Current_State, out_5);
  and _0_100 (_0_100_out, not_21_out, out_3, not_22_out, not_23_out);
  and _1_100 (_1_100_out, Input, out_3, not_24_out, not_25_out);
  D_Flip_Flop State_bit_3 (.clk(clock_1_out), .D(S1_out), .Q(out_5));  // open: Qn, preset, en, reset
  D_Flip_Flop State_bit_2 (.clk(clock_1_out), .D(S2_out), .Q(Current_State));  // open: Qn, preset, en, reset
  D_Flip_Flop State_bit_1 (.clk(clock_1_out), .D(S3_out), .Q(out_3));  // open: Qn, preset, en, reset
  buf or_1 (Output, _1_100_out);  // OR_Gate
  buf S3 (S3_out, _0_011_out);  // OR_Gate
  or S2 (S2_out, _0_001_out, _0_010_out);
  or S1 (S1_out, _1_000_out, _1_010_out, _1_011_out, _1_100_out, _0_010_out, _1_001_out);
endmodule
